// Logisim project project.circ as structural Verilog
module main (
  output [31:0] INSTRUCTION,
  output [7:0] out_2
);

  wire clock_1_out, RESET_out;

  Clock clock_1 (.out(clock_1_out));
  Button RESET (.out(RESET_out));
  ROM #(.dataWidth(32)) rom_1 (.addr(out_2), .data(INSTRUCTION));
  PC pc_1 (.clk(clock_1_out), .reset(RESET_out), .out_3(out_2));

  // Notes on the sheet:
  //   contents of rom_1 (hex, n*v repeats v):
  //   100000 1000
endmodule

module PC (
  input  clk,
  input  reset,
  output [7:0] out_3
);

  wire [31:0] adder_1_out, register_1_q;

  Adder #(.width(32)) adder_1 (
    .a(32'h4), .b({register_1_q[31:10], out_3, register_1_q[1:0]}), .out(adder_1_out));  // open: cin, cout
  Register #(.width(32)) register_1 (
    .D(adder_1_out), .clk(clk), .Q({register_1_q[31:10], out_3, register_1_q[1:0]}), .clr(reset));  // open: en
endmodule

// MUXREG1
module BancoDeRegistradores (
  input  [2:0] READ1,
  input  [2:0] READ2,
  input  clear,
  input  clk,
  input  [31:0] Data,
  input  [2:0] WriteEnable,
  input  enaREGwrite,
  output [31:0] RD1,
  output [31:0] RD2
);

  wire enaREG0, enaREG1, enaREG2, enaREG3, enaREG4, enaREG5, enaREG6, enaREG7;
  wire [31:0] demultiplexer_1_out0, demultiplexer_1_out1, demultiplexer_1_out2, demultiplexer_1_out3,
       demultiplexer_1_out4, demultiplexer_1_out5, demultiplexer_1_out6, demultiplexer_1_out7, MUXREG0,
       MUXREG1, MUXREG2, MUXREG3, MUXREG4, MUXREG5, MUXREG6, MUXREG7;

  Multiplexer #(.select(3), .width(32)) multiplexer_1 (
    .in0(MUXREG0), .in1(MUXREG1), .in2(MUXREG2), .in3(MUXREG3), .in4(MUXREG4), .in5(MUXREG5), .in6(MUXREG6),
    .in7(MUXREG7), .out(RD1), .sel(READ1));
  Multiplexer #(.select(3), .width(32)) multiplexer_2 (
    .in0(MUXREG0), .in1(MUXREG1), .in2(MUXREG2), .in3(MUXREG3), .in4(MUXREG4), .in5(MUXREG5), .in6(MUXREG6),
    .in7(MUXREG7), .out(RD2), .sel(READ2));
  Demultiplexer #(.select(3), .width(32)) demultiplexer_1 (
    .out0(demultiplexer_1_out0), .out1(demultiplexer_1_out1), .out2(demultiplexer_1_out2),
    .out3(demultiplexer_1_out3), .out4(demultiplexer_1_out4), .out5(demultiplexer_1_out5),
    .out6(demultiplexer_1_out6), .out7(demultiplexer_1_out7), .in(Data), .sel(WriteEnable));
  Demultiplexer #(.select(3)) demultiplexer_2 (
    .out0(enaREG0), .out1(enaREG1), .out2(enaREG2), .out3(enaREG3), .out4(enaREG4), .out5(enaREG5),
    .out6(enaREG6), .out7(enaREG7), .in(enaREGwrite), .sel(WriteEnable));
  Register #(.width(32)) REG0 (.D(demultiplexer_1_out0), .en(enaREG0), .clk(clk), .Q(MUXREG0), .clr(clear));
  Register #(.width(32)) REG1 (.D(demultiplexer_1_out1), .en(enaREG1), .clk(clk), .Q(MUXREG1), .clr(clear));
  Register #(.width(32)) REG2 (.D(demultiplexer_1_out2), .en(enaREG2), .clk(clk), .Q(MUXREG2), .clr(clear));
  Register #(.width(32)) REG3 (.D(demultiplexer_1_out3), .en(enaREG3), .clk(clk), .Q(MUXREG3), .clr(clear));
  Register #(.width(32)) REG4 (.D(demultiplexer_1_out4), .en(enaREG4), .clk(clk), .Q(MUXREG4), .clr(clear));
  Register #(.width(32)) REG5 (.D(demultiplexer_1_out5), .en(enaREG5), .clk(clk), .Q(MUXREG5), .clr(clear));
  Register #(.width(32)) REG6 (.D(demultiplexer_1_out6), .en(enaREG6), .clk(clk), .Q(MUXREG6), .clr(clear));
  Register #(.width(32)) REG7 (.D(demultiplexer_1_out7), .en(enaREG7), .clk(clk), .Q(MUXREG7));  // open: clr
endmodule
